# Fritzing sketch Wireless SB 2.0 (saved by Fritzing 0.9.2b)

parts:
  Part1 = Arduino Nano (Rev3.0) (ICSP)
  Part2 = NRF24L01
  S1 = Pushbutton [package="[THT]"]
  S2 = Pushbutton [package="[THT]"]
  S3 = Pushbutton [package="[THT]"]
  S4 = Pushbutton [package="[THT]"]
  S5 = Pushbutton [package="[THT]"]
  S6 = Pushbutton [package="[THT]"]
  S7 = Pushbutton [package="[THT]"]
  S8 = Pushbutton [package="[THT]"]
  S9 = Pushbutton [package="[THT]"]
  S10 = Pushbutton [package="[THT]"]
  S11 = Pushbutton [package="[THT]"]
  S12 = Pushbutton [package="[THT]"]
  S13 = Pushbutton [package="[THT]"]
  S14 = Pushbutton [package="[THT]"]
  S15 = Pushbutton [package="[THT]"]
  S16 = Pushbutton [package="[THT]"]
  U2 = LIPO-2000mAh [package=lipo-2000]
  Part3 = Micro Lipo Charger
  R1 = Resistor [tolerance=±5% resistance=330 package=THT]
  R2 = Resistor [tolerance=±5% resistance=100 package=THT]
  LED1 = RGB LED - (4 legs) [package="5 mm [THT]"]

nets:
  GND: Part1.GND, Part2.GND, U2.-, Part3.GND, R2.Pin_0
  N1: Part1.D2, S1.Pin_3, S1.Pin_4, S2.Pin_3, S2.Pin_4, S3.Pin_3, S3.Pin_4, S4.Pin_3, S4.Pin_4
  N2: Part1.D3, S5.Pin_3, S5.Pin_4, S6.Pin_3, S6.Pin_4, S7.Pin_3, S7.Pin_4, S8.Pin_3, S8.Pin_4
  N3: Part1.D4, S10.Pin_3, S10.Pin_4, S11.Pin_3, S11.Pin_4, S13.Pin_3, S13.Pin_4, S14.Pin_3, S14.Pin_4
  N4: Part1.D5, S9.Pin_3, S9.Pin_4, S12.Pin_3, S12.Pin_4, S15.Pin_3, S15.Pin_4, S16.Pin_3, S16.Pin_4
  N5: Part1.D7, LED1.red_cathode
  N6: Part1.D8, LED1.green_cathode
  N7: Part1.D9, Part2.CE
  N8: Part1.D10, Part2.CSN
  N9: Part1.D11/MOSI, Part2.MOSI
  N10: Part1.D12/MISO, Part2.MISO
  VIN: Part1.VIN, Part3.5V
  N11: Part1.5V, LED1.common_anode
  N12: Part1.A7, LED1.blue_cathode
  N13: Part1.A6, R1.Pin_0, R2.Pin_1
  N14: Part1.A3, S3.Pin_1, S3.Pin_2, S5.Pin_2, S11.Pin_2, S15.Pin_1, S15.Pin_2
  N15: Part1.A2, S2.Pin_1, S2.Pin_2, S6.Pin_2, S10.Pin_2, S16.Pin_1, S16.Pin_2
  N16: Part1.A1, S1.Pin_2, S7.Pin_2, S12.Pin_1, S12.Pin_2, S14.Pin_2
  N17: Part1.A0, S4.Pin_1, S4.Pin_2, S8.Pin_2, S9.Pin_1, S9.Pin_2, S13.Pin_2
  3V3: Part1.3V3, Part2.VCC
  N18: Part1.D13/SCK, Part2.SCK
  N19: U2.+, Part3.VBAT

custom parts:
  Micro Lipo Charger: Oh so handy, this little lipo charger is so small and easy to use you can keep it on your desk or mount it easily into any project! Simply plug it via any MicroUSB cable into a USB port and a 3.7V/4.2V lithium polymer or lithium ion rechargeable battery into the JST plug on the other end. There are two LEDs - one red and one green. While charging, the red LED is lit. When the battery is fully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
